# Fritzing sketch WemosD1_DHT22-BMP180 (saved by Fritzing 0.9.3b)
circuit board: 8.46667cm x 5.64444cm
breadboards: 1

parts:
  DHT1 = DHT22 Humidity and Temperature Sensor
  R1 = Resistor [tolerance=±5% resistance=10k package="2512 [SMD]"]
  Componente1 = Barometric Pressure Sensor - BMP180 Breakout (GY-68)
  WeMos_D1_Mini1 = WeMos D1 Mini  # not connected
  Grove1 = Grove OLED 128x96
  WeMos_D1_Mini_Battery_Shield1 = WeMos D1 Mini Battery Shield  # not connected

nets (from the breadboard view):
  VCC: DHT1.VDD, R1.Pin_0, Componente1.VCC, Grove1.VCC
  N1: DHT1.DATA, R1.Pin_1
  GND: DHT1.GND, Componente1.GND, Grove1.GND
  N2: Componente1.SCL, Grove1.SCL
  N3: Componente1.SDA, Grove1.SDA
