# Fritzing sketch WemosD1_DHT22 (saved by Fritzing 0.9.3b)
breadboards: 1

parts:
  DHT1 = DHT22 Humidity and Temperature Sensor
  R1 = Resistor [tolerance=±5% resistance=10k package="2512 [SMD]"]
  WeMos_D1_Mini1 = WeMos D1 Mini

nets:
  VDD: DHT1.VDD, R1.Pin_1, WeMos_D1_Mini1.3V3
  N1: DHT1.DATA, R1.Pin_0, WeMos_D1_Mini1.D5
  N2: DHT1.GND, WeMos_D1_Mini1.G

notes:
  [scrivi qui le tue note]
